// Digital circuit frontpanel.dig as structural Verilog
module frontpanel (
  input  [15:0] value,
  input  [1:0] dest,
  input  [1:0] src,
  input  tworeg,
  output [15:0] R0,
  output [15:0] R1,
  output [15:0] R2,
  output [15:0] R3,
  output [15:0] L,
  output [1:0] rs,
  output [1:0] rd,
  output [15:0] R,
  output [3:0] PC,
  output [15:0] target,
  output [1:0] rd_2,
  output [1:0] rs_2,
  output [1:0] rd_3,
  output [15:0] R_2
);

  wire add, add_out, advance_out, assembler_1_store_clk, decoder_1_p1, decoder_1_p2, decoder_1_p6,
       execute_1_p4, fetch_1_p8, jump, jump_out, mode_out, move, move_out, pmshim_1_c, pmshim_1_l, pmshim_1_s;
  wire [3:0] pmshim_1_a;
  wire [31:0] assembler_1_inst, pmshim_1_d, Program_d;

  Button u_add (.out(add_out));
  Button u_move (.out(move_out));
  Button u_jump (.out(jump_out));
  LED programming (.in(mode_out));
  DipSwitch mode (.out(mode_out));
  assembler assembler_1 (
    .prog(mode_out), .value(value), .dest(dest), .src(src), .tworeg(tworeg), .add(add_out), .move(move_out),
    .jump(jump_out), .inst(assembler_1_inst), .store_clk(assembler_1_store_clk));
  pmshim pmshim_1 (
    .pc(PC), .i_in(assembler_1_inst), .s_c(assembler_1_store_clk), .A(pmshim_1_a), .D(pmshim_1_d),
    .s(pmshim_1_s), .C(pmshim_1_c), .L(pmshim_1_l));
  EEPROMDualPort #(.AddrBits(4), .isProgramMemory("true"), .Bits(32)) Program (
    .A(pmshim_1_a), .Din(pmshim_1_d), .str(pmshim_1_s), .C(pmshim_1_c), .ld(pmshim_1_l), .D(Program_d));
  Button advance (.out(advance_out));
  // fetch fetch_1: pin names not known; wires that end beside it: mode_out, assembler_1_inst, Program_d, advance_out, R, jump, PC, fetch_1_p8
  LED jump_2 (.in(jump));
  LED move_2 (.in(move));
  LED add_2 (.in(add));
  // decoder decoder_1: pin names not known; wires that end beside it: decoder_1_p1, decoder_1_p2, fetch_1_p8, rs, rd, decoder_1_p6, L, R, move, add, jump
  // execute execute_1: pin names not known; wires that end beside it: decoder_1_p6, L, R, execute_1_p4
  // regfile regfile_1: pin names not known; wires that end beside it: rs, rd, execute_1_p4, advance_out, decoder_1_p1, decoder_1_p2, R0, R1, R2, R3

  assign R_2 = R;
  assign rd_2 = rd;
  assign rd_3 = rd;
  assign rs_2 = rs;
  assign target = R;

  // Notes on the sheet:
  //   rj45 Creates
  //   Fibonacci
  //   0: R2 = R2 + 1
  //   1: R2 = R2 + R1
  //   2: R3 = R2 + 0
  //   3: R1 = R1 + R2
  //   4: R3 = R1 + 0
  //   5: jump 1
  //   contents of Program (hex, n*v repeats v):
  //   220001,8120000,e230000,8210000,e130000,7000001
  //   PC =
  //   R
  //   =
  //   ( R
  //   )
  //   +
endmodule
